// Logisim project Q3-navigation.circ as structural Verilog
module navigation (
  input  [1:0] in_1,
  input  in_2,
  input  in_3,
  output out_4,
  output out_5
);

  wire not_1_out;
  wire [2:0] register_1_q;
  wire [3:0] n1_1_a2;

  _1 u_1_1 (
    .a(register_1_q[0]), .b(register_1_q[1]), .c(register_1_q[2]), .A_2(in_1[1]), .a2(n1_1_a2[0]),
    .B_2(in_1[0]), .d(out_4), .b2(n1_1_a2[1]), .c2(n1_1_a2[2]), .d2(n1_1_a2[3]));
  Register #(.width(4)) register_1 (.D(n1_1_a2), .en(1'b1), .Q({out_4, register_1_q}), .clk(in_2), .clr(in_3));
  not not_1 (not_1_out, register_1_q[0]);
  and and_1 (out_5, register_1_q[2], register_1_q[1], not_1_out);
endmodule

module _1 (
  input  a,
  input  b,
  input  c,
  input  A_2,
  input  B_2,
  input  d,
  output a2,
  output b2,
  output c2,
  output d2
);

  wire and_1_out, and_2_out, and_3_out, and_4_out, and_5_out, and_6_out, and_7_out, and_8_out, and_9_out,
       and_10_out, and_11_out, and_12_out, and_13_out, and_14_out, and_15_out, and_16_out, and_17_out,
       and_18_out, and_19_out, not_1_out, not_2_out, not_3_out, not_4_out, not_5_out, not_6_out, not_7_out,
       not_8_out, not_9_out, not_10_out, not_11_out, not_12_out, not_13_out, not_14_out, not_15_out,
       not_16_out, not_17_out, not_18_out, not_19_out, not_20_out, not_21_out, not_22_out, not_23_out,
       not_24_out, not_25_out, not_26_out, not_27_out, not_28_out, not_29_out, not_30_out, not_31_out,
       not_32_out, not_33_out, not_34_out, not_35_out, not_36_out, not_37_out, not_38_out, not_39_out,
       not_40_out, not_41_out, not_42_out, not_43_out, not_44_out, not_45_out, not_46_out, not_47_out,
       not_48_out, not_49_out, not_50_out, not_51_out, not_52_out, not_53_out, not_54_out, not_55_out,
       not_56_out;

  not not_1 (not_1_out, a);
  not not_2 (not_2_out, b);
  not not_3 (not_3_out, A_2);
  not not_4 (not_4_out, B_2);
  not not_5 (not_5_out, b);
  not not_6 (not_6_out, c);
  not not_7 (not_7_out, A_2);
  not not_8 (not_8_out, B_2);
  not not_9 (not_9_out, b);
  not not_10 (not_10_out, c);
  not not_11 (not_11_out, a);
  not not_12 (not_12_out, b);
  not not_13 (not_13_out, A_2);
  not not_14 (not_14_out, a);
  not not_15 (not_15_out, c);
  not not_16 (not_16_out, A_2);
  not not_17 (not_17_out, a);
  not not_18 (not_18_out, c);
  not not_19 (not_19_out, B_2);
  not not_20 (not_20_out, b);
  not not_21 (not_21_out, c);
  not not_22 (not_22_out, A_2);
  not not_23 (not_23_out, a);
  not not_24 (not_24_out, c);
  not not_25 (not_25_out, A_2);
  not not_26 (not_26_out, B_2);
  not not_27 (not_27_out, a);
  not not_28 (not_28_out, b);
  not not_29 (not_29_out, a);
  not not_30 (not_30_out, c);
  not not_31 (not_31_out, b);
  not not_32 (not_32_out, c);
  not not_33 (not_33_out, A_2);
  not not_34 (not_34_out, b);
  not not_35 (not_35_out, c);
  not not_36 (not_36_out, B_2);
  not not_37 (not_37_out, a);
  not not_38 (not_38_out, b);
  not not_39 (not_39_out, c);
  not not_40 (not_40_out, a);
  not not_41 (not_41_out, b);
  not not_42 (not_42_out, c);
  not not_43 (not_43_out, a);
  not not_44 (not_44_out, b);
  not not_45 (not_45_out, a);
  not not_46 (not_46_out, c);
  not not_47 (not_47_out, B_2);
  not not_48 (not_48_out, a);
  not not_49 (not_49_out, c);
  not not_50 (not_50_out, A_2);
  not not_51 (not_51_out, b);
  not not_52 (not_52_out, c);
  not not_53 (not_53_out, b);
  not not_54 (not_54_out, c);
  not not_55 (not_55_out, A_2);
  not not_56 (not_56_out, B_2);
  and and_1 (and_1_out, not_1_out, not_2_out, c, not_3_out, not_4_out);
  and and_2 (and_2_out, a, not_5_out, not_6_out, not_7_out, not_8_out);
  and and_3 (and_3_out, a, not_9_out, not_10_out, A_2, B_2);
  and and_4 (and_4_out, not_11_out, not_12_out, c, not_13_out, B_2);
  and and_5 (and_5_out, not_14_out, b, not_15_out, not_16_out);
  and and_6 (and_6_out, not_17_out, b, not_18_out, not_19_out);
  and and_7 (and_7_out, a, not_20_out, not_21_out, not_22_out, B_2);
  and and_8 (and_8_out, not_23_out, not_24_out, not_25_out, not_26_out);
  and and_9 (and_9_out, not_27_out, not_28_out, c, A_2, B_2);
  and and_10 (and_10_out, not_29_out, b, not_30_out, A_2, B_2);
  and and_11 (and_11_out, a, not_31_out, not_32_out, not_33_out, B_2);
  and and_12 (and_12_out, a, not_34_out, not_35_out, A_2, not_36_out);
  and and_13 (and_13_out, not_37_out, not_38_out, not_39_out, A_2);
  and and_14 (and_14_out, not_40_out, not_41_out, not_42_out, B_2);
  and and_15 (and_15_out, not_43_out, not_44_out, c, A_2, B_2);
  and and_16 (and_16_out, not_45_out, b, not_46_out, A_2, not_47_out);
  and and_17 (and_17_out, not_48_out, b, not_49_out, not_50_out, B_2);
  and and_18 (and_18_out, a, not_51_out, not_52_out, A_2, B_2);
  and and_19 (and_19_out, a, not_53_out, not_54_out, not_55_out, not_56_out);
  or or_1 (a2, and_1_out, and_2_out, and_3_out);
  or or_2 (b2, and_4_out, and_5_out, and_6_out, and_7_out);
  or or_3 (c2, and_8_out, and_9_out, and_10_out, and_11_out, and_12_out);
  or or_4 (d2, and_13_out, and_14_out, and_15_out, and_16_out, and_17_out, and_18_out, and_19_out);
endmodule
