// Logisim project Q4-fsm.circ as structural Verilog: 3 circuits, main circuit fsm
module fsm (
  input  [1:0] in_1,
  input  in_2,
  output out_3
);

  wire clock_1_out;
  wire [1:0] n1_1_d2, register_1_q;

  _1 u_1_1 (
    .a(in_1[1]), .b(in_1[0]), .c2(register_1_q[1]), .d(register_1_q[0]), .r(in_2), .c(n1_1_d2[1]),
    .d2(n1_1_d2[0]));
  Clock clock_1 (.out(clock_1_out));
  Register #(.width(2)) register_1 (.D(n1_1_d2), .en(1'b1), .Q(register_1_q), .clk(clock_1_out));  // open: clr
  _2 u_2_1 (.a(in_1[1]), .b(in_1[0]), .c(register_1_q[1]), .d(register_1_q[0]), .s(out_3));
endmodule

module _1 (
  input  a,
  input  b,
  input  c2,
  input  d,
  input  r,
  output c,
  output d2
);

  wire and_1_out, and_2_out, and_3_out, and_4_out, not_1_out, not_2_out, not_3_out, not_4_out, not_5_out,
       not_6_out, not_7_out, not_8_out, not_9_out, not_10_out, not_11_out, not_12_out, not_13_out;

  not not_1 (not_1_out, a);
  not not_2 (not_2_out, b);
  not not_3 (not_3_out, c2);
  not not_4 (not_4_out, r);
  not not_5 (not_5_out, b);
  not not_6 (not_6_out, c2);
  not not_7 (not_7_out, r);
  not not_8 (not_8_out, a);
  not not_9 (not_9_out, c2);
  not not_10 (not_10_out, r);
  not not_11 (not_11_out, a);
  not not_12 (not_12_out, d);
  not not_13 (not_13_out, r);
  and and_1 (and_1_out, not_1_out, not_2_out, not_3_out, d, not_4_out);
  and and_2 (and_2_out, a, not_5_out, not_6_out, d, not_7_out);
  and and_3 (and_3_out, not_8_out, b, not_9_out, not_10_out);
  and and_4 (and_4_out, not_11_out, b, c2, not_12_out, not_13_out);
  or or_1 (c, and_1_out, and_2_out);
  or or_2 (d2, and_3_out, and_4_out);
endmodule

module _2 (
  input  a,
  input  b,
  input  c,
  input  d,
  output s
);

  wire and_1_out, and_2_out, not_1_out, not_2_out, not_3_out, not_4_out, not_5_out;

  not not_1 (not_1_out, a);
  not not_2 (not_2_out, b);
  not not_3 (not_3_out, d);
  not not_4 (not_4_out, b);
  not not_5 (not_5_out, d);
  and and_1 (and_1_out, not_1_out, not_2_out, c, not_3_out);
  or or_1 (s, and_1_out, and_2_out);
  and and_2 (and_2_out, a, not_4_out, c, not_5_out);
endmodule
