// Logisim project p0_1.circ as structural Verilog: 3 circuits, main circuit main
module main (
  input  [7:0] in_1,
  input  [3:0] in_2,
  output [10:0] out_3
);

  wire [2:0] n4bit_2_1_c, n4bit_2_2_c, n4bit_2_3_c, n4bit_2_4_c, n4bit_2_5_c, n4bit_2_7_c, n4bit_2_8_c;
  wire [3:0] bit_extender_2_out, bit_extender_3_out, bit_extender_4_out, bit_extender_5_out,
       bit_extender_6_out, bit_extender_7_out, bit_extender_8_out, shifter_2_out, shifter_3_out,
       shifter_4_out, shifter_5_out, shifter_6_out, shifter_7_out, tunn;
  wire [10:0] bit_extender_1_out, shifter_1_out;

  assign bit_extender_1_out = {{3{1'b0}}, in_1};  // Bit_Extender bit_extender_1
  Shifter #(.width(11), .shift("rl")) shifter_1 (.in(bit_extender_1_out), .\dist (4'b0011), .out(shifter_1_out));
  // Probe on shifter_1_out
  // Probe on shifter_1_out[6]
  _4bit_2 u_4bit_2_1 (.A(shifter_1_out[10:7]), .B(in_2), .C(n4bit_2_1_c));
  assign bit_extender_2_out = {{1{shifter_1_out[6]}}, n4bit_2_1_c};  // Bit_Extender bit_extender_2
  // Probe on n4bit_2_1_c
  // Probe on bit_extender_2_out
  _4bit_2 u_4bit_2_2 (.A(tunn), .B(in_2), .C(n4bit_2_2_c));
  Shifter #(.width(4), .shift("rl")) shifter_2 (.in(bit_extender_2_out), .\dist (2'b01), .out(shifter_2_out));
  assign bit_extender_3_out = {{1{shifter_1_out[1]}}, n4bit_2_2_c};  // Bit_Extender bit_extender_3
  _4bit_2 u_4bit_2_3 (.A(shifter_2_out), .B(in_2), .C(n4bit_2_3_c));
  Shifter #(.width(4), .shift("rl")) shifter_3 (.in(bit_extender_3_out), .\dist (2'b01), .out(shifter_3_out));
  assign bit_extender_4_out = {{1{shifter_1_out[5]}}, n4bit_2_3_c};  // Bit_Extender bit_extender_4
  _4bit_2 u_4bit_2_4 (.A(shifter_3_out), .B(in_2), .C(n4bit_2_4_c));
  Shifter #(.width(4), .shift("rl")) shifter_4 (.in(bit_extender_4_out), .\dist (2'b01), .out(shifter_4_out));
  assign bit_extender_5_out = {{1{shifter_1_out[0]}}, n4bit_2_4_c};  // Bit_Extender bit_extender_5
  _4bit_2 u_4bit_2_5 (.A(shifter_4_out), .B(in_2), .C(n4bit_2_5_c));
  Shifter #(.width(4), .shift("rl")) shifter_5 (.in(bit_extender_5_out), .\dist (2'b01), .out(shifter_5_out));
  assign bit_extender_6_out = {{1{shifter_1_out[4]}}, n4bit_2_5_c};  // Bit_Extender bit_extender_6
  _4bit_2 u_4bit_2_6 (.A(shifter_5_out), .B(in_2), .C(out_3[2:0]));
  Shifter #(.width(4), .shift("rl")) shifter_6 (.in(bit_extender_6_out), .\dist (2'b01), .out(shifter_6_out));
  _4bit_2 u_4bit_2_7 (.A(shifter_6_out), .B(in_2), .C(n4bit_2_7_c));
  assign bit_extender_7_out = {{1{shifter_1_out[3]}}, n4bit_2_7_c};  // Bit_Extender bit_extender_7
  Shifter #(.width(4), .shift("rl")) shifter_7 (.in(bit_extender_7_out), .\dist (2'b01), .out(shifter_7_out));
  _4bit_2 u_4bit_2_8 (.A(shifter_7_out), .B(in_2), .C(n4bit_2_8_c));
  assign bit_extender_8_out = {{1{shifter_1_out[2]}}, n4bit_2_8_c};  // Bit_Extender bit_extender_8
  Shifter #(.width(4), .shift("rl")) shifter_8 (.in(bit_extender_8_out), .\dist (2'b01), .out(tunn));

  assign out_3[10:3] = in_1;

  // Other names for the same wires on the sheet: div[3:0] = in_2
endmodule

module _4bit_2 (
  input  [3:0] A,
  input  [3:0] B,
  output [2:0] C
);

  wire [2:0] and_1_out, and_2_out, bit_extender_1_out, not_1_out, xor_1_out;

  xor xor_1 (xor_1_out[0], A[0], B[0]);
  xor xor_2 (xor_1_out[1], A[1], B[1]);
  xor xor_3 (xor_1_out[2], A[2], B[2]);
  // XOR_Gate xor_4 has open pins: in0=A[3], in1=B[3], out=open
  assign bit_extender_1_out = {{2{A[3]}}, A[3]};  // Bit_Extender bit_extender_1
  // Probe on bit_extender_1_out
  assign and_1_out = xor_1_out & bit_extender_1_out;  // AND_Gate and_1, 3 bits wide
  assign not_1_out = ~bit_extender_1_out;  // NOT_Gate not_1, 3 bits wide
  assign and_2_out = A[2:0] & not_1_out;  // AND_Gate and_2, 3 bits wide
  assign C = and_1_out | and_2_out;  // OR_Gate or_1, 3 bits wide

  // Other names for the same wires on the sheet: a_t[2:0] = A[2:0]
endmodule

module CRC (
  input  [7:0] in_1,
  input  [3:0] in_2,
  output [10:0] out_3
);

  wire [2:0] n4bit_2_1_c, n4bit_2_2_c, n4bit_2_3_c, n4bit_2_4_c, n4bit_2_5_c, n4bit_2_7_c, n4bit_2_8_c;
  wire [3:0] bit_extender_2_out, bit_extender_3_out, bit_extender_4_out, bit_extender_5_out,
       bit_extender_6_out, bit_extender_7_out, bit_extender_8_out, shifter_2_out, shifter_3_out,
       shifter_4_out, shifter_5_out, shifter_6_out, shifter_7_out, tunn;
  wire [10:0] bit_extender_1_out, shifter_1_out;

  assign bit_extender_1_out = {{3{1'b0}}, in_1};  // Bit_Extender bit_extender_1
  Shifter #(.width(11), .shift("rl")) shifter_1 (.in(bit_extender_1_out), .\dist (4'b0011), .out(shifter_1_out));
  // Probe on shifter_1_out
  // Probe on shifter_1_out[6]
  _4bit_2 u_4bit_2_1 (.A(shifter_1_out[10:7]), .B(in_2), .C(n4bit_2_1_c));
  assign bit_extender_2_out = {{1{shifter_1_out[6]}}, n4bit_2_1_c};  // Bit_Extender bit_extender_2
  // Probe on n4bit_2_1_c
  // Probe on bit_extender_2_out
  _4bit_2 u_4bit_2_2 (.A(tunn), .B(in_2), .C(n4bit_2_2_c));
  Shifter #(.width(4), .shift("rl")) shifter_2 (.in(bit_extender_2_out), .\dist (2'b01), .out(shifter_2_out));
  assign bit_extender_3_out = {{1{shifter_1_out[1]}}, n4bit_2_2_c};  // Bit_Extender bit_extender_3
  _4bit_2 u_4bit_2_3 (.A(shifter_2_out), .B(in_2), .C(n4bit_2_3_c));
  Shifter #(.width(4), .shift("rl")) shifter_3 (.in(bit_extender_3_out), .\dist (2'b01), .out(shifter_3_out));
  assign bit_extender_4_out = {{1{shifter_1_out[5]}}, n4bit_2_3_c};  // Bit_Extender bit_extender_4
  _4bit_2 u_4bit_2_4 (.A(shifter_3_out), .B(in_2), .C(n4bit_2_4_c));
  Shifter #(.width(4), .shift("rl")) shifter_4 (.in(bit_extender_4_out), .\dist (2'b01), .out(shifter_4_out));
  assign bit_extender_5_out = {{1{shifter_1_out[0]}}, n4bit_2_4_c};  // Bit_Extender bit_extender_5
  _4bit_2 u_4bit_2_5 (.A(shifter_4_out), .B(in_2), .C(n4bit_2_5_c));
  Shifter #(.width(4), .shift("rl")) shifter_5 (.in(bit_extender_5_out), .\dist (2'b01), .out(shifter_5_out));
  assign bit_extender_6_out = {{1{shifter_1_out[4]}}, n4bit_2_5_c};  // Bit_Extender bit_extender_6
  _4bit_2 u_4bit_2_6 (.A(shifter_5_out), .B(in_2), .C(out_3[2:0]));
  Shifter #(.width(4), .shift("rl")) shifter_6 (.in(bit_extender_6_out), .\dist (2'b01), .out(shifter_6_out));
  _4bit_2 u_4bit_2_7 (.A(shifter_6_out), .B(in_2), .C(n4bit_2_7_c));
  assign bit_extender_7_out = {{1{shifter_1_out[3]}}, n4bit_2_7_c};  // Bit_Extender bit_extender_7
  Shifter #(.width(4), .shift("rl")) shifter_7 (.in(bit_extender_7_out), .\dist (2'b01), .out(shifter_7_out));
  _4bit_2 u_4bit_2_8 (.A(shifter_7_out), .B(in_2), .C(n4bit_2_8_c));
  assign bit_extender_8_out = {{1{shifter_1_out[2]}}, n4bit_2_8_c};  // Bit_Extender bit_extender_8
  Shifter #(.width(4), .shift("rl")) shifter_8 (.in(bit_extender_8_out), .\dist (2'b01), .out(tunn));

  assign out_3[10:3] = in_1;

  // Other names for the same wires on the sheet: div[3:0] = in_2
endmodule
