// Logisim project p0_2.circ as structural Verilog: 5 circuits, main circuit main
module main (
  input  in_1,
  input  reset,
  input  WE,
  input  [2:0] A1,
  input  [2:0] A2,
  input  [2:0] A3,
  input  A3xx,
  input  [31:0] WD,
  output [31:0] out_9,
  output [31:0] out_10
);

  wire and_1_out, decoder_1_out0, decoder_1_out1, decoder_1_out2, decoder_1_out3, decoder_1_out4,
       decoder_1_out5, decoder_1_out6, decoder_1_out7;
  wire [31:0] register_1_q, register_2_q, register_3_q, register_4_q, register_5_q, register_6_q,
       register_7_q, register_8_q;

  and and_1 (and_1_out, WE, A3xx);
  Decoder #(.select(3)) decoder_1 (
    .out0(decoder_1_out0), .out1(decoder_1_out1), .out2(decoder_1_out2), .out3(decoder_1_out3),
    .out4(decoder_1_out4), .out5(decoder_1_out5), .out6(decoder_1_out6), .out7(decoder_1_out7), .sel(A3),
    .en(and_1_out));
  // Probe on decoder_1_out7
  Register #(.width(32)) register_1 (.D(WD), .en(decoder_1_out1), .Q(register_1_q), .clk(in_1), .clr(reset));
  Register #(.width(32)) register_2 (.D(WD), .en(decoder_1_out0), .Q(register_2_q), .clk(in_1), .clr(reset));
  Register #(.width(32)) register_3 (.D(WD), .en(decoder_1_out5), .Q(register_3_q), .clk(in_1), .clr(reset));
  Register #(.width(32)) register_4 (.D(WD), .en(decoder_1_out4), .Q(register_4_q), .clk(in_1), .clr(reset));
  Register #(.width(32)) register_5 (.D(WD), .en(decoder_1_out2), .Q(register_5_q), .clk(in_1), .clr(reset));
  Register #(.width(32)) register_6 (.D(WD), .en(decoder_1_out6), .Q(register_6_q), .clk(in_1), .clr(reset));
  Register #(.width(32)) register_7 (.D(WD), .en(decoder_1_out3), .Q(register_7_q), .clk(in_1), .clr(reset));
  Register #(.width(32)) register_8 (.D(WD), .en(decoder_1_out7), .Q(register_8_q), .clk(in_1), .clr(reset));
  Multiplexer #(.select(3), .width(32)) multiplexer_1 (
    .in0(register_2_q), .in1(register_1_q), .in2(register_5_q), .in3(register_7_q), .in4(register_4_q),
    .in5(register_3_q), .in6(register_6_q), .in7(register_8_q), .out(out_9), .sel(A1));  // open: en
  Multiplexer #(.select(3), .width(32)) multiplexer_2 (
    .in0(register_2_q), .in1(register_1_q), .in2(register_5_q), .in3(register_7_q), .in4(register_4_q),
    .in5(register_3_q), .in6(register_6_q), .in7(register_8_q), .out(out_10), .sel(A2));  // open: en

  // Other names for the same wires on the sheet: a[2:0] = A1; b[2:0] = A2
endmodule

// we
module grf (
  input  clk,
  input  reset,
  input  WE,
  input  [4:0] A1,
  input  [4:0] A2,
  input  [4:0] A3,
  input  [31:0] WD,
  output [31:0] RD1,
  output [31:0] RD2
);

  wire decoder_1_out0, decoder_1_out1, decoder_1_out2, decoder_1_out3;
  wire [31:0] little_0_1_out_9, little_0_1_out_10, test_1_out_9, test_1_out_10, test_2_out_9, test_2_out_10,
       test_3_out_9, test_3_out_10;

  Decoder #(.select(2)) decoder_1 (
    .out0(decoder_1_out0), .out1(decoder_1_out1), .out2(decoder_1_out2), .out3(decoder_1_out3), .sel(A3[4:3]));  // open: en
  little_0 little_0_1 (
    .A1(A1[2:0]), .A2(A2[2:0]), .A3xx(decoder_1_out0), .A3(A3[2:0]), .WD(WD), .clk(clk), .reset(reset),
    .WE(WE), .out_9(little_0_1_out_9), .out_10(little_0_1_out_10));
  // Probe on reset
  test test_1 (
    .A1(A1[2:0]), .A2(A2[2:0]), .A3xx(decoder_1_out1), .A3(A3[2:0]), .WD(WD), .in_1(clk), .reset(reset),
    .WE(WE), .out_9(test_1_out_9), .out_10(test_1_out_10));
  test test_2 (
    .A1(A1[2:0]), .A2(A2[2:0]), .A3xx(decoder_1_out2), .A3(A3[2:0]), .WD(WD), .in_1(clk), .reset(reset),
    .WE(WE), .out_9(test_2_out_9), .out_10(test_2_out_10));
  test test_3 (
    .A1(A1[2:0]), .A2(A2[2:0]), .A3xx(decoder_1_out3), .A3(A3[2:0]), .WD(WD), .in_1(clk), .reset(reset),
    .WE(WE), .out_9(test_3_out_9), .out_10(test_3_out_10));
  Multiplexer #(.select(2), .width(32)) multiplexer_1 (
    .in0(little_0_1_out_9), .in1(test_1_out_9), .in2(test_2_out_9), .in3(test_3_out_9), .out(RD1),
    .sel(A1[4:3]));  // open: en
  Multiplexer #(.select(2), .width(32)) multiplexer_2 (
    .in0(little_0_1_out_10), .in1(test_1_out_10), .in2(test_2_out_10), .in3(test_3_out_10), .out(RD2),
    .sel(A2[4:3]));  // open: en
endmodule

module little_0 (
  input  reset,
  input  clk,
  input  WE,
  input  [2:0] A1,
  input  [2:0] A2,
  input  A3xx,
  input  [2:0] A3,
  input  [31:0] WD,
  output [31:0] out_9,
  output [31:0] out_10
);

  wire and_1_out, decoder_1_out0, decoder_1_out1, decoder_1_out2, decoder_1_out3, decoder_1_out4,
       decoder_1_out5, decoder_1_out6, decoder_1_out7, not_1_out;
  wire [3:0] bit_extender_1_out;
  wire [31:0] register_1_q, register_2_q, register_3_q, register_4_q, register_5_q, register_6_q,
       register_7_q, register_8_q;

  and and_1 (and_1_out, WE, A3xx);
  not not_1 (not_1_out, and_1_out);
  assign bit_extender_1_out = {{1{not_1_out}}, A3};  // Bit_Extender bit_extender_1
  Decoder #(.select(4)) decoder_1 (
    .out0(decoder_1_out0), .out1(decoder_1_out1), .out2(decoder_1_out2), .out3(decoder_1_out3),
    .out4(decoder_1_out4), .out5(decoder_1_out5), .out6(decoder_1_out6), .out7(decoder_1_out7),
    .sel(bit_extender_1_out));  // open: out8, out9, out10, out11, out12, out13, out14, out15, en
  Register #(.width(32)) register_1 (.en(decoder_1_out0), .Q(register_1_q), .clk(clk), .clr(reset));  // open: D
  Register #(.width(32)) register_2 (.D(WD), .en(decoder_1_out4), .Q(register_2_q), .clk(clk), .clr(reset));
  Register #(.width(32)) register_3 (.D(WD), .en(decoder_1_out1), .Q(register_3_q), .clk(clk), .clr(reset));
  Register #(.width(32)) register_4 (.D(WD), .en(decoder_1_out5), .Q(register_4_q), .clk(clk), .clr(reset));
  Register #(.width(32)) register_5 (.D(WD), .en(decoder_1_out2), .Q(register_5_q), .clk(clk), .clr(reset));
  Register #(.width(32)) register_6 (.D(WD), .en(decoder_1_out6), .Q(register_6_q), .clk(clk), .clr(reset));
  Register #(.width(32)) register_7 (.D(WD), .en(decoder_1_out3), .Q(register_7_q), .clk(clk), .clr(reset));
  Register #(.width(32)) register_8 (.D(WD), .en(decoder_1_out7), .Q(register_8_q), .clk(clk), .clr(reset));
  Multiplexer #(.select(3), .width(32)) multiplexer_1 (
    .in0(register_1_q), .in1(register_3_q), .in2(register_5_q), .in3(register_7_q), .in4(register_2_q),
    .in5(register_4_q), .in6(register_6_q), .in7(register_8_q), .out(out_9), .sel(A1));  // open: en
  Multiplexer #(.select(3), .width(32)) multiplexer_2 (
    .in0(register_1_q), .in1(register_3_q), .in2(register_5_q), .in3(register_7_q), .in4(register_2_q),
    .in5(register_4_q), .in6(register_6_q), .in7(register_8_q), .out(out_10), .sel(A2));  // open: en

  // Other names for the same wires on the sheet: a[2:0] = A1; b[2:0] = A2
endmodule

module test (
  input  in_1,
  input  reset,
  input  WE,
  input  [2:0] A1,
  input  [2:0] A2,
  input  A3xx,
  input  [2:0] A3,
  input  [31:0] WD,
  output [31:0] out_9,
  output [31:0] out_10
);

  wire and_1_out, decoder_1_out0, decoder_1_out1, decoder_1_out2, decoder_1_out3, decoder_1_out4,
       decoder_1_out5, decoder_1_out6, decoder_1_out7, not_1_out;
  wire [3:0] bit_extender_1_out;
  wire [31:0] register_1_q, register_2_q, register_3_q, register_4_q, register_5_q, register_6_q,
       register_7_q, register_8_q;

  not not_1 (not_1_out, and_1_out);
  and and_1 (and_1_out, WE, A3xx);
  assign bit_extender_1_out = {{1{not_1_out}}, A3};  // Bit_Extender bit_extender_1
  Decoder #(.select(4)) decoder_1 (
    .out0(decoder_1_out0), .out1(decoder_1_out1), .out2(decoder_1_out2), .out3(decoder_1_out3),
    .out4(decoder_1_out4), .out5(decoder_1_out5), .out6(decoder_1_out6), .out7(decoder_1_out7),
    .sel(bit_extender_1_out));  // open: out8, out9, out10, out11, out12, out13, out14, out15, en
  Register #(.width(32)) register_1 (.D(WD), .en(decoder_1_out0), .Q(register_1_q), .clk(in_1), .clr(reset));
  Register #(.width(32)) register_2 (.D(WD), .en(decoder_1_out1), .Q(register_2_q), .clk(in_1), .clr(reset));
  Register #(.width(32)) register_3 (.D(WD), .en(decoder_1_out5), .Q(register_3_q), .clk(in_1), .clr(reset));
  Register #(.width(32)) register_4 (.D(WD), .en(decoder_1_out4), .Q(register_4_q), .clk(in_1), .clr(reset));
  Register #(.width(32)) register_5 (.D(WD), .en(decoder_1_out2), .Q(register_5_q), .clk(in_1), .clr(reset));
  Register #(.width(32)) register_6 (.D(WD), .en(decoder_1_out6), .Q(register_6_q), .clk(in_1), .clr(reset));
  Register #(.width(32)) register_7 (.D(WD), .en(decoder_1_out3), .Q(register_7_q), .clk(in_1), .clr(reset));
  Register #(.width(32)) register_8 (.D(WD), .en(decoder_1_out7), .Q(register_8_q), .clk(in_1), .clr(reset));
  Multiplexer #(.select(3), .width(32)) multiplexer_1 (
    .in0(register_1_q), .in1(register_2_q), .in2(register_5_q), .in3(register_7_q), .in4(register_4_q),
    .in5(register_3_q), .in6(register_6_q), .in7(register_8_q), .out(out_9), .sel(A1));  // open: en
  Multiplexer #(.select(3), .width(32)) multiplexer_2 (
    .in0(register_1_q), .in1(register_2_q), .in2(register_5_q), .in3(register_7_q), .in4(register_4_q),
    .in5(register_3_q), .in6(register_6_q), .in7(register_8_q), .out(out_10), .sel(A2));  // open: en

  // Other names for the same wires on the sheet: a[2:0] = A1; b[2:0] = A2
endmodule

module test1 (
  input  in_1,
  input  [7:0] in_2,
  output [7:0] out_3
);

  wire clock_1_out, undriven;

  Register register_1 (.D(in_2), .en(undriven), .Q(out_3), .clk(clock_1_out));  // open: clr
  Clock clock_1 (.out(clock_1_out));
endmodule
