// Logisim project p0_3.circ as structural Verilog
// arrive
module navigation (
  input  [1:0] dir_1_0,
  input  clk,
  input  reset,
  output arrive,
  output hit
);

  wire clock_1_out_6, clock_1_out_7, clock_1_out_8, hit_1_hit, not_1_out, not_2_out, test_1_s0_2,
       test_1_s1_2, test_1_s2_2;

  test test_1 (
    .s0(clock_1_out_6), .s1(clock_1_out_7), .s2(clock_1_out_8), .dir0(dir_1_0[1]), .dir1(dir_1_0[0]),
    .s0_2(test_1_s0_2), .s1_2(test_1_s1_2), .s2_2(test_1_s2_2));
  clock clock_1 (
    .in_2(clk), .in_3(test_1_s0_2), .in_4(test_1_s1_2), .in_5(test_1_s2_2), .in_1(reset),
    .out_6(clock_1_out_6), .out_7(clock_1_out_7), .out_8(clock_1_out_8));
  hit hit_1 (
    .s0(clock_1_out_6), .s1(clock_1_out_7), .s2(clock_1_out_8), .dir0(dir_1_0[1]), .dir1(dir_1_0[0]),
    .hit(hit_1_hit));
  not not_1 (not_1_out, clock_1_out_7);
  and and_1 (arrive, clock_1_out_6, not_1_out, not_2_out);
  not not_2 (not_2_out, clock_1_out_8);
  Register #(.width(1)) register_1 (.D(hit_1_hit), .Q(hit), .clk(clk), .clr(reset));  // open: en
endmodule

module clock (
  input  in_1,
  input  in_2,
  input  in_3,
  input  in_4,
  input  in_5,
  output out_6,
  output out_7,
  output out_8
);

  Register #(.width(1)) register_1 (.D(in_3), .Q(out_6), .clk(in_2), .clr(in_1));  // open: en
  Register #(.width(1)) register_2 (.D(in_4), .Q(out_7), .clk(in_2), .clr(in_1));  // open: en
  Register #(.width(1)) register_3 (.D(in_5), .Q(out_8), .clk(in_2), .clr(in_1));  // open: en
endmodule

module hit (
  input  s0,
  input  s1,
  input  s2,
  input  dir0,
  input  dir1,
  output hit
);

  wire and_1_out, and_2_out, and_3_out, and_4_out, and_5_out, not_1_out, not_2_out, not_3_out, not_4_out,
       not_5_out, not_6_out, not_7_out, not_8_out, not_9_out, not_10_out, not_11_out;

  not not_1 (not_1_out, s0);
  not not_2 (not_2_out, s2);
  not not_3 (not_3_out, dir0);
  not not_4 (not_4_out, s0);
  not not_5 (not_5_out, s1);
  not not_6 (not_6_out, s2);
  not not_7 (not_7_out, s0);
  not not_8 (not_8_out, s2);
  not not_9 (not_9_out, dir1);
  not not_10 (not_10_out, dir0);
  not not_11 (not_11_out, dir1);
  and and_1 (and_1_out, not_1_out, not_2_out, not_3_out, dir1);
  and and_2 (and_2_out, not_4_out, not_5_out, not_6_out, dir0);
  and and_3 (and_3_out, not_7_out, not_8_out, dir0, not_9_out);
  and and_4 (and_4_out, s2, dir0, dir1);
  and and_5 (and_5_out, s1, s2, not_10_out, not_11_out);
  or or_1 (hit, and_1_out, and_2_out, and_3_out, and_4_out, and_5_out);
endmodule

module test (
  input  s0,
  input  s1,
  input  s2,
  input  dir0,
  input  dir1,
  output s0_2,
  output s1_2,
  output s2_2
);

  wire and_1_out, and_2_out, and_3_out, and_4_out, and_5_out, and_6_out, and_7_out, and_8_out, and_9_out,
       and_10_out, and_11_out, not_1_out, not_2_out, not_3_out, not_4_out, not_5_out, not_6_out, not_7_out,
       not_8_out, not_9_out, not_10_out, not_11_out, not_12_out, not_13_out, not_14_out, not_15_out,
       not_16_out, not_17_out;

  not not_1 (not_1_out, s2);
  not not_2 (not_2_out, dir0);
  not not_3 (not_3_out, dir1);
  not not_4 (not_4_out, dir0);
  not not_5 (not_5_out, s1);
  not not_6 (not_6_out, dir0);
  not not_7 (not_7_out, dir0);
  not not_8 (not_8_out, dir1);
  not not_9 (not_9_out, s2);
  not not_10 (not_10_out, dir0);
  not not_11 (not_11_out, s2);
  not not_12 (not_12_out, dir1);
  not not_13 (not_13_out, s0);
  not not_14 (not_14_out, s1);
  not not_15 (not_15_out, dir0);
  not not_16 (not_16_out, dir1);
  not not_17 (not_17_out, dir1);
  and and_1 (and_1_out, s1, not_1_out, not_2_out, not_3_out);
  and and_2 (and_2_out, s1, s2, not_4_out, dir1);
  and and_3 (and_3_out, not_5_out, s2, not_6_out);
  and and_4 (and_4_out, s2, not_7_out, not_8_out);
  and and_5 (and_5_out, s1, not_9_out, not_10_out, dir1);
  and and_6 (and_6_out, s1, not_11_out, dir0, not_12_out);
  and and_7 (and_7_out, s1, s2, dir0, dir1);
  and and_8 (and_8_out, not_13_out, not_14_out, not_15_out, not_16_out);
  and and_9 (and_9_out, s2, dir0, dir1);
  and and_10 (and_10_out, s1, dir0, dir1);
  and and_11 (and_11_out, s1, s2, not_17_out);
  or or_1 (s0_2, and_1_out, and_2_out);
  or or_2 (s1_2, and_3_out, and_4_out, and_5_out, and_6_out, and_7_out);
  or or_3 (s2_2, and_8_out, and_9_out, and_10_out, and_11_out);
endmodule
