// Logisim project p0_4.circ as structural Verilog: 5 circuits, main circuit main
module main (
  input  CLR,
  input  [1:0] In,
  output Z
);

  wire clk_1_out_4, clk_1_out_5, clock_1_out, not_1_out, test_1_s0_2, test_1_s1_2;

  Clock clock_1 (.out(clock_1_out));
  test test_1 (
    .s0(clk_1_out_4), .s1(clk_1_out_5), .p0(In[1]), .p1(In[0]), .CLR(CLR), .s0_2(test_1_s0_2),
    .s1_2(test_1_s1_2));
  clk clk_1 (.clk(clock_1_out), .s0(test_1_s0_2), .s1(test_1_s1_2), .out_4(clk_1_out_4), .out_5(clk_1_out_5));
  not not_1 (not_1_out, In[0]);
  and and_1 (Z, not_1_out, clk_1_out_4, clk_1_out_5);
endmodule

module test (
  input  s0,
  input  s1,
  input  p0,
  input  p1,
  input  CLR,
  output s0_2,
  output s1_2
);

  wire and_1_out, and_2_out, and_3_out, and_4_out, and_5_out, and_6_out, and_7_out, not_1_out, not_2_out,
       not_3_out, not_4_out, not_5_out, not_6_out, not_7_out, not_8_out, not_9_out, not_10_out, not_11_out,
       not_12_out, not_13_out, not_14_out, or_1_out, or_2_out;

  not not_1 (not_1_out, CLR);
  not not_2 (not_2_out, s0);
  not not_3 (not_3_out, p0);
  not not_4 (not_4_out, s0);
  not not_5 (not_5_out, p1);
  not not_6 (not_6_out, s1);
  not not_7 (not_7_out, p1);
  not not_8 (not_8_out, s1);
  not not_9 (not_9_out, p0);
  not not_10 (not_10_out, s0);
  not not_11 (not_11_out, p1);
  not not_12 (not_12_out, s1);
  not not_13 (not_13_out, p1);
  not not_14 (not_14_out, p0);
  and and_1 (and_1_out, not_2_out, s1, not_3_out);
  or or_1 (or_1_out, and_1_out, and_2_out, and_3_out);
  and and_2 (and_2_out, not_4_out, s1, not_5_out);
  and and_3 (and_3_out, s0, not_6_out, not_7_out);
  and and_4 (and_4_out, not_8_out, not_9_out, p1);
  and and_5 (and_5_out, not_10_out, s1, not_11_out);
  and and_6 (and_6_out, s0, not_12_out, not_13_out);
  and and_7 (and_7_out, s0, not_14_out, p1);
  or or_2 (or_2_out, and_4_out, and_5_out, and_6_out, and_7_out);
  and and_8 (s0_2, not_1_out, or_1_out);
  and and_9 (s1_2, not_1_out, or_2_out);
endmodule

module clk (
  input  clk,
  input  s0,
  input  s1,
  output out_4,
  output out_5
);

  Register #(.width(1)) register_1 (.D(s0), .Q(out_4), .clk(clk));  // open: en, clr
  Register #(.width(1)) register_2 (.D(s1), .Q(out_5), .clk(clk));  // open: en, clr
endmodule

module \output  (
  input  s0,
  input  s1,
  input  p0,
  input  p1,
  output Z
);

  wire not_1_out;

  and and_1 (Z, s0, s1, not_1_out);
  not not_1 (not_1_out, p1);
endmodule

module fsm (
  input  CLR,
  input  [1:0] In,
  output Z
);

  wire clk_1_out_4, clk_1_out_5, clock_1_out, not_1_out, test_1_s0_2, test_1_s1_2;

  Clock clock_1 (.out(clock_1_out));
  test test_1 (
    .s0(clk_1_out_4), .s1(clk_1_out_5), .p0(In[1]), .p1(In[0]), .CLR(CLR), .s0_2(test_1_s0_2),
    .s1_2(test_1_s1_2));
  clk clk_1 (.clk(clock_1_out), .s0(test_1_s0_2), .s1(test_1_s1_2), .out_4(clk_1_out_4), .out_5(clk_1_out_5));
  not not_1 (not_1_out, In[0]);
  and and_1 (Z, not_1_out, clk_1_out_4, clk_1_out_5);
endmodule
