// Logisim project cpu1.circ as structural Verilog: 9 circuits, main circuit main
module main (
  input  reset,
  output [31:0] out_2,
  output out_3,
  output [4:0] out_4,
  output [31:0] out_5,
  output out_6,
  output [4:0] out_7,
  output [31:0] out_8
);

  wire alu_1_zero, Alusrc, branch, clk_out, controller_1_aluop0, controller_1_aluop1, extensi, luireg,
       memread, memtoreg, pcsrc, regdst;
  wire [1:0] Aluctrl;
  wire [31:0] alu_1_result, dm_1_rd, extend_1_out_3, grf2_1_rd1, multiplexer_2_out, multiplexer_3_out,
       shifter_2_out, shiftleft;

  Clock clk (.out(clk_out));
  IFU ifu_1 (.shift_left2(shiftleft), .PCsrc(pcsrc), .clk(clk_out), .RD(out_2), .reset(reset));
  // Probe on out_2[31:26]
  extend extend_1 (.in_1(out_2[15:0]), .in_2(extensi), .out_3(extend_1_out_3));
  Multiplexer #(.width(5)) multiplexer_1 (
    .in0(out_2[20:16]), .in1(out_2[15:11]), .out(out_4), .sel(regdst));  // open: en
  Controller controller_1 (
    .opcode(out_2[31:26]), .regdst(regdst), .branch(branch), .memtoreg(memtoreg), .regwrite(out_3),
    .memread(memread), .memwrite(out_6), .alusrc(Alusrc), .luireg(luireg), .aluop1(controller_1_aluop1),
    .extensi(extensi), .aluop0(controller_1_aluop0));
  GRF2 grf2_1 (
    .RA1(out_2[25:21]), .WA(out_4), .clk(clk_out), .regWrite(out_3), .WD(out_5), .reset(reset),
    .RA2(out_2[20:16]), .RD1(grf2_1_rd1), .RD2(out_8));
  Shifter #(.width(32)) shifter_1 (.in(extend_1_out_3), .\dist (5'b00010), .out(shiftleft));
  Multiplexer #(.width(32)) multiplexer_2 (
    .in0(out_8), .in1(extend_1_out_3), .out(multiplexer_2_out), .sel(Alusrc));  // open: en
  ALUcontrol alucontrol_1 (
    .func(out_2[1]), .ALUop1(controller_1_aluop1), .ALUop0(controller_1_aluop0), .out1(Aluctrl[1]),
    .out0(Aluctrl[0]));
  ALU alu_1 (
    .ALUctrl(Aluctrl), .a(grf2_1_rd1), .b(multiplexer_2_out), .zero(alu_1_zero),
    .result({alu_1_result[31:7], out_7, alu_1_result[1:0]}));
  and and_1 (pcsrc, branch, alu_1_zero);
  DM dm_1 (.A(out_7), .WD(out_8), .reset(reset), .RD(dm_1_rd), .RE(memread), .WE(out_6), .clk(clk_out));
  Shifter #(.width(32)) shifter_2 (.in(extend_1_out_3), .\dist (5'b10000), .out(shifter_2_out));
  // Probe on out_4
  // Probe on out_7
  Multiplexer #(.width(32)) multiplexer_3 (
    .in0(dm_1_rd), .in1({alu_1_result[31:7], out_7, alu_1_result[1:0]}), .out(multiplexer_3_out),
    .sel(memtoreg));  // open: en
  Multiplexer #(.width(32)) multiplexer_4 (
    .in0(multiplexer_3_out), .in1(shifter_2_out), .out(out_5), .sel(luireg));  // open: en
  // Probe on out_2
  // Probe on out_5
  // Probe on out_8

  // Other names for the same wires on the sheet: memaddr[4:0] = out_7; imm16[15:0] = out_2[15:0]; instr[31:0] = out_2;
  //   func = out_2[1]; rd[4:0] = out_2[15:11]; memdata[31:0] = out_8; memwrite = out_6; opcode[5:0] = out_2[31:26];
  //   regaddr[4:0] = out_4; regdata[31:0] = out_5; regwrite = out_3; rs[4:0] = out_2[25:21]; rt[4:0] = out_2[20:16]
endmodule

module ALU (
  input  [1:0] ALUctrl,
  input  [31:0] a,
  input  [31:0] b,
  output zero,
  output [31:0] result
);

  wire [31:0] adder_1_out, multiplexer_1_out, negator_1_out, or_1_out;

  Negator #(.width(32)) negator_1 (.in(b), .out(negator_1_out));
  Multiplexer #(.width(32)) multiplexer_1 (
    .in0(b), .in1(negator_1_out), .out(multiplexer_1_out), .sel(ALUctrl[1]));  // open: en
  assign or_1_out = a | b;  // OR_Gate or_1, 32 bits wide
  Adder #(.width(32)) adder_1 (.a(a), .b(multiplexer_1_out), .out(adder_1_out));  // open: cin, cout
  Multiplexer #(.width(32)) multiplexer_2 (
    .in0(or_1_out), .in1(adder_1_out), .out(result), .sel(ALUctrl[0]));  // open: en
  Comparator #(.width(32)) comparator_1 (.a(a), .b(b), .eq(zero));  // open: gt, lt
endmodule

module IFU (
  input  [31:0] shift_left2,
  input  PCsrc,
  input  clk,
  input  reset,
  output [31:0] RD
);

  wire [31:0] adder_1_out, adder_2_out, multiplexer_1_out, pc_q;

  Register #(.width(32)) pc (.D(multiplexer_1_out), .Q(pc_q), .clk(clk), .clr(reset));  // open: en
  Adder #(.width(32)) adder_1 (.a(pc_q), .b(32'h4), .out(adder_1_out));  // open: cin, cout
  Adder #(.width(32)) adder_2 (.a(adder_1_out), .b(shift_left2), .out(adder_2_out));  // open: cin, cout
  ROM #(.addrWidth(5), .dataWidth(32)) rom_1 (.addr(pc_q[6:2]), .data(RD));  // open: sel
  Multiplexer #(.width(32)) multiplexer_1 (
    .in0(adder_1_out), .in1(adder_2_out), .out(multiplexer_1_out), .sel(PCsrc));  // open: en

  // Notes on the sheet:
  //   contents of rom_1 (hex, n*v repeats v):
  //   3404006f 3405007b 10850000 3405006f 1085fffb
endmodule

module GRF (
  input  Regwrite,
  input  [31:0] WD,
  input  clk,
  input  [7:0] _5_32decoder,
  input  reset,
  output [31:0] out_6,
  output [31:0] out_7,
  output [31:0] out_8,
  output [31:0] out_9,
  output [31:0] out_10,
  output [31:0] out_11,
  output [31:0] out_12,
  output [31:0] out_13
);

  wire and_1_out, and_2_out, and_3_out, and_4_out, and_5_out, and_6_out, and_7_out, and_8_out;

  and and_1 (and_1_out, _5_32decoder[0], Regwrite);
  and and_2 (and_2_out, _5_32decoder[1], Regwrite);
  and and_3 (and_3_out, _5_32decoder[2], Regwrite);
  and and_4 (and_4_out, _5_32decoder[3], Regwrite);
  and and_5 (and_5_out, _5_32decoder[4], Regwrite);
  and and_6 (and_6_out, _5_32decoder[5], Regwrite);
  and and_7 (and_7_out, _5_32decoder[6], Regwrite);
  and and_8 (and_8_out, _5_32decoder[7], Regwrite);
  Register #(.width(32)) _0 (.D(WD), .en(and_1_out), .Q(out_6), .clk(clk), .clr(reset));
  Register #(.width(32)) _1 (.D(WD), .en(and_2_out), .Q(out_7), .clk(clk), .clr(reset));
  Register #(.width(32)) _2 (.D(WD), .en(and_3_out), .Q(out_8), .clk(clk), .clr(reset));
  Register #(.width(32)) _3 (.D(WD), .en(and_4_out), .Q(out_9), .clk(clk), .clr(reset));
  Register #(.width(32)) register_1 (.D(WD), .en(and_5_out), .Q(out_10), .clk(clk), .clr(reset));
  Register #(.width(32)) register_2 (.D(WD), .en(and_6_out), .Q(out_11), .clk(clk), .clr(reset));
  Register #(.width(32)) register_3 (.D(WD), .en(and_7_out), .Q(out_12), .clk(clk), .clr(reset));
  Register #(.width(32)) register_4 (.D(WD), .en(and_8_out), .Q(out_13), .clk(clk), .clr(reset));
endmodule

module GRF2 (
  input  [4:0] RA1,
  input  [4:0] WA,
  input  clk,
  input  regWrite,
  input  [31:0] WD,
  input  reset,
  input  [4:0] RA2,
  output [31:0] RD1,
  output [31:0] RD2
);

  wire decoder_1_out0;
  wire [6:0] decoder_1_out1;
  wire [7:0] decoder_1_out8, decoder_1_out16, decoder_1_out24;
  wire [31:0] grf_1_out_6, grf_1_out_7, grf_1_out_8, grf_1_out_9, grf_1_out_10, grf_1_out_11, grf_1_out_12,
       grf_1_out_13, grf_2_out_6, grf_2_out_7, grf_2_out_8, grf_2_out_9, grf_2_out_10, grf_2_out_11,
       grf_2_out_12, grf_2_out_13, grf_3_out_6, grf_3_out_7, grf_3_out_8, grf_3_out_9, grf_3_out_10,
       grf_3_out_11, grf_3_out_12, grf_3_out_13, grf_4_out_6, grf_4_out_7, grf_4_out_8, grf_4_out_9,
       grf_4_out_10, grf_4_out_11, grf_4_out_12, grf_4_out_13;

  Decoder #(.select(5)) decoder_1 (
    .out0(decoder_1_out0), .out1(decoder_1_out1[0]), .out2(decoder_1_out1[1]), .out3(decoder_1_out1[2]),
    .out4(decoder_1_out1[3]), .out5(decoder_1_out1[4]), .out6(decoder_1_out1[5]), .out7(decoder_1_out1[6]),
    .out8(decoder_1_out8[0]), .out9(decoder_1_out8[1]), .out10(decoder_1_out8[2]), .out11(decoder_1_out8[3]),
    .out12(decoder_1_out8[4]), .out13(decoder_1_out8[5]), .out14(decoder_1_out8[6]),
    .out15(decoder_1_out8[7]), .out16(decoder_1_out16[0]), .out17(decoder_1_out16[1]),
    .out18(decoder_1_out16[2]), .out19(decoder_1_out16[3]), .out20(decoder_1_out16[4]),
    .out21(decoder_1_out16[5]), .out22(decoder_1_out16[6]), .out23(decoder_1_out16[7]),
    .out24(decoder_1_out24[0]), .out25(decoder_1_out24[1]), .out26(decoder_1_out24[3]),
    .out27(decoder_1_out24[3]), .out28(decoder_1_out24[4]), .out29(decoder_1_out24[5]),
    .out30(decoder_1_out24[6]), .out31(decoder_1_out24[7]), .sel(WA));  // open: en
  // Probe on {decoder_1_out1, 1'b0}
  GRF grf_1 (
    .Regwrite(regWrite), .WD(WD), .clk(clk), ._5_32decoder({decoder_1_out1, 1'b0}), .reset(reset),
    .out_6(grf_1_out_6), .out_7(grf_1_out_7), .out_8(grf_1_out_8), .out_9(grf_1_out_9),
    .out_10(grf_1_out_10), .out_11(grf_1_out_11), .out_12(grf_1_out_12), .out_13(grf_1_out_13));
  GRF grf_2 (
    .Regwrite(regWrite), .WD(WD), .clk(clk), ._5_32decoder(decoder_1_out8), .reset(reset),
    .out_6(grf_2_out_6), .out_7(grf_2_out_7), .out_8(grf_2_out_8), .out_9(grf_2_out_9),
    .out_10(grf_2_out_10), .out_11(grf_2_out_11), .out_12(grf_2_out_12), .out_13(grf_2_out_13));
  GRF grf_3 (
    .Regwrite(regWrite), .WD(WD), .clk(clk), ._5_32decoder(decoder_1_out16), .reset(reset),
    .out_6(grf_3_out_6), .out_7(grf_3_out_7), .out_8(grf_3_out_8), .out_9(grf_3_out_9),
    .out_10(grf_3_out_10), .out_11(grf_3_out_11), .out_12(grf_3_out_12), .out_13(grf_3_out_13));
  GRF grf_4 (
    .Regwrite(regWrite), .WD(WD), .clk(clk),
    ._5_32decoder({decoder_1_out24[7:3], decoder_1_out24[3], decoder_1_out24[1:0]}), .reset(reset),
    .out_6(grf_4_out_6), .out_7(grf_4_out_7), .out_8(grf_4_out_8), .out_9(grf_4_out_9),
    .out_10(grf_4_out_10), .out_11(grf_4_out_11), .out_12(grf_4_out_12), .out_13(grf_4_out_13));
  Multiplexer #(.select(5), .width(32)) multiplexer_1 (
    .in0(grf_1_out_6), .in1(grf_1_out_7), .in2(grf_1_out_8), .in3(grf_1_out_9), .in4(grf_1_out_10),
    .in5(grf_1_out_11), .in6(grf_1_out_12), .in7(grf_1_out_13), .in8(grf_2_out_6), .in9(grf_2_out_7),
    .in10(grf_2_out_8), .in11(grf_2_out_9), .in12(grf_2_out_10), .in13(grf_2_out_11), .in14(grf_2_out_12),
    .in15(grf_2_out_13), .in16(grf_3_out_6), .in17(grf_3_out_7), .in18(grf_3_out_8), .in19(grf_3_out_9),
    .in20(grf_3_out_10), .in21(grf_3_out_11), .in22(grf_3_out_12), .in23(grf_3_out_13), .in24(grf_4_out_6),
    .in25(grf_4_out_7), .in26(grf_4_out_8), .in27(grf_4_out_9), .in28(grf_4_out_10), .in29(grf_4_out_11),
    .in30(grf_4_out_12), .in31(grf_4_out_13), .out(RD1), .sel(RA1));  // open: en
  Multiplexer #(.select(5), .width(32)) multiplexer_2 (
    .in0(grf_1_out_6), .in1(grf_1_out_7), .in2(grf_1_out_8), .in3(grf_1_out_9), .in4(grf_1_out_10),
    .in5(grf_1_out_11), .in6(grf_1_out_12), .in7(grf_1_out_13), .in8(grf_2_out_6), .in9(grf_2_out_7),
    .in10(grf_2_out_8), .in11(grf_2_out_9), .in12(grf_2_out_10), .in13(grf_2_out_11), .in14(grf_2_out_12),
    .in15(grf_2_out_13), .in16(grf_3_out_6), .in17(grf_3_out_7), .in18(grf_3_out_8), .in19(grf_3_out_9),
    .in20(grf_3_out_10), .in21(grf_3_out_11), .in22(grf_3_out_12), .in23(grf_3_out_13), .in24(grf_4_out_6),
    .in25(grf_4_out_7), .in26(grf_4_out_8), .in27(grf_4_out_9), .in28(grf_4_out_10), .in29(grf_4_out_11),
    .in30(grf_4_out_12), .in31(grf_4_out_13), .out(RD2), .sel(RA2));  // open: en
endmodule

module DM (
  input  RE,
  input  WE,
  input  [4:0] A,
  input  [31:0] WD,
  input  reset,
  input  clk,
  output [31:0] RD
);

  RAM #(.addrWidth(5), .dataWidth(32), .bus("separate")) ram_1 (
    .addr(A), .din(WD), .data(RD), .str(WE), .clk(clk), .ld(RE), .clr(reset));  // open: sel
endmodule

module Controller (
  input  [5:0] opcode,
  output regdst,
  output branch,
  output memtoreg,
  output regwrite,
  output memread,
  output memwrite,
  output alusrc,
  output luireg,
  output aluop1,
  output extensi,
  output aluop0
);

  wire ori_out;

  and R (regdst, ~opcode[0], ~opcode[1], ~opcode[2], ~opcode[4], ~opcode[5], ~opcode[3]);  // AND_Gate
  and lw (memread, opcode[0], opcode[1], ~opcode[2], ~opcode[3], ~opcode[4], opcode[5]);  // AND_Gate
  and sw (memwrite, opcode[0], opcode[1], ~opcode[2], opcode[3], ~opcode[4], opcode[5]);  // AND_Gate
  and beq (branch, ~opcode[0], ~opcode[1], opcode[2], ~opcode[3], ~opcode[4], ~opcode[5]);  // AND_Gate
  and ori (ori_out, opcode[0], ~opcode[1], opcode[2], opcode[3], ~opcode[4], ~opcode[5]);  // AND_Gate
  and lui (luireg, opcode[0], opcode[1], opcode[2], opcode[3], ~opcode[4], ~opcode[5]);  // AND_Gate
  or or_1 (memtoreg, regdst, ori_out, luireg);
  or or_2 (regwrite, regdst, memread, ori_out, luireg);
  or or_3 (alusrc, memread, memwrite, ori_out, luireg);
  or or_4 (aluop1, regdst, ori_out);
  or or_5 (extensi, memread, memwrite, branch);
  or or_6 (aluop0, branch, ori_out);
endmodule

module extend (
  input  [15:0] in_1,
  input  in_2,
  output [31:0] out_3
);

  wire [31:0] bit_extender_1_out, bit_extender_2_out;

  assign bit_extender_1_out = {{16{1'b0}}, in_1};  // Bit_Extender bit_extender_1
  assign bit_extender_2_out = {{16{in_1[15]}}, in_1};  // Bit_Extender bit_extender_2
  Multiplexer #(.width(32)) multiplexer_1 (
    .in0(bit_extender_1_out), .in1(bit_extender_2_out), .out(out_3), .sel(in_2));  // open: en
endmodule

module ALUcontrol (
  input  func,
  input  ALUop1,
  input  ALUop0,
  output out0,
  output out1
);

  wire and_1_out, and_2_out, not_1_out, not_2_out, not_3_out, not_4_out;

  not not_1 (not_1_out, ALUop1);
  not not_2 (not_2_out, ALUop0);
  not not_3 (not_3_out, ALUop1);
  not not_4 (not_4_out, ALUop0);
  and and_1 (and_1_out, not_1_out, ALUop0);
  and and_2 (and_2_out, func, ALUop1, not_2_out);
  or or_1 (out0, not_3_out, not_4_out);
  or or_2 (out1, and_1_out, and_2_out);
endmodule
